// Logisim project 16bit reg.circ as structural Verilog: 1 circuit, main circuit main
module main (
  input  load,
  input  INC,
  input  [15:0] \input ,
  input  CLR,
  input  CLOCK,
  output [15:0] \output 
);

  wire and_1_out, and_2_out, and_3_out, and_4_out, and_5_out, and_6_out, and_7_out, and_8_out, and_9_out,
       and_10_out, and_11_out, and_12_out, and_13_out, and_14_out, and_15_out, and_16_out, and_17_out,
       and_18_out, and_19_out, and_20_out, and_21_out, and_22_out, and_23_out, and_24_out, and_25_out,
       and_26_out, and_27_out, and_28_out, and_29_out, and_30_out, and_31_out, and_32_out, and_33_out,
       and_34_out, and_35_out, and_36_out, and_37_out, and_38_out, and_39_out, and_40_out, and_41_out,
       and_42_out, and_43_out, and_44_out, and_45_out, and_46_out, and_47_out, and_48_out, not_1_out,
       not_2_out, not_3_out, not_4_out, not_5_out, not_6_out, not_7_out, not_8_out, not_9_out, not_10_out,
       not_11_out, not_12_out, not_13_out, not_14_out, not_15_out, not_16_out, not_17_out, or_1_out,
       or_2_out, or_3_out, or_4_out, or_5_out, or_6_out, or_7_out, or_8_out, or_9_out, or_10_out, or_11_out,
       or_12_out, or_13_out, or_14_out, or_15_out, or_16_out, or_17_out, or_18_out, or_19_out, or_20_out,
       or_21_out, or_22_out, or_23_out, or_24_out, or_25_out, or_26_out, or_27_out, or_28_out, or_29_out,
       or_30_out, or_31_out, or_32_out;

  not not_1 (not_1_out, \input [0]);
  not not_2 (not_2_out, \input [1]);
  not not_3 (not_3_out, \input [2]);
  not not_4 (not_4_out, \input [3]);
  not not_5 (not_5_out, \input [4]);
  not not_6 (not_6_out, \input [5]);
  not not_7 (not_7_out, \input [6]);
  not not_8 (not_8_out, \input [7]);
  not not_9 (not_9_out, \input [8]);
  not not_10 (not_10_out, \input [9]);
  not not_11 (not_11_out, \input [10]);
  not not_12 (not_12_out, \input [11]);
  not not_13 (not_13_out, \input [12]);
  not not_14 (not_14_out, \input [13]);
  not not_15 (not_15_out, \input [14]);
  not not_16 (not_16_out, \input [15]);
  not not_17 (not_17_out, load);
  and and_1 (and_1_out, not_17_out, INC);
  and and_2 (and_2_out, load, \input [0]);
  and and_3 (and_3_out, load, not_1_out);
  and and_4 (and_4_out, load, \input [1]);
  and and_5 (and_5_out, and_1_out, \output [0]);
  and and_6 (and_6_out, load, not_2_out);
  and and_7 (and_7_out, load, \input [2]);
  and and_8 (and_8_out, and_5_out, \output [1]);
  and and_9 (and_9_out, load, not_3_out);
  and and_10 (and_10_out, load, \input [3]);
  and and_11 (and_11_out, load, not_4_out);
  and and_12 (and_12_out, load, \input [4]);
  and and_13 (and_13_out, load, not_5_out);
  and and_14 (and_14_out, load, \input [5]);
  and and_15 (and_15_out, load, not_6_out);
  and and_16 (and_16_out, load, \input [6]);
  and and_17 (and_17_out, load, not_7_out);
  and and_18 (and_18_out, load, \input [7]);
  and and_19 (and_19_out, load, not_8_out);
  and and_20 (and_20_out, load, \input [8]);
  and and_21 (and_21_out, load, not_9_out);
  and and_22 (and_22_out, load, \input [9]);
  and and_23 (and_23_out, load, not_10_out);
  and and_24 (and_24_out, load, \input [10]);
  and and_25 (and_25_out, load, not_11_out);
  and and_26 (and_26_out, load, \input [11]);
  and and_27 (and_27_out, load, not_12_out);
  and and_28 (and_28_out, load, \input [12]);
  and and_29 (and_29_out, load, not_13_out);
  and and_30 (and_30_out, load, \input [13]);
  and and_31 (and_31_out, load, not_14_out);
  and and_32 (and_32_out, load, \input [14]);
  and and_33 (and_33_out, load, not_15_out);
  and and_34 (and_34_out, load, \input [15]);
  and and_35 (and_35_out, load, not_16_out);
  and and_36 (and_36_out, and_8_out, \output [2]);
  and and_37 (and_37_out, and_36_out, \output [3]);
  and and_38 (and_38_out, and_37_out, \output [4]);
  and and_39 (and_39_out, and_38_out, \output [5]);
  and and_40 (and_40_out, and_39_out, \output [6]);
  and and_41 (and_41_out, and_40_out, \output [7]);
  and and_42 (and_42_out, and_41_out, \output [8]);
  and and_43 (and_43_out, and_42_out, \output [9]);
  and and_44 (and_44_out, and_43_out, \output [10]);
  and and_45 (and_45_out, and_44_out, \output [11]);
  and and_46 (and_46_out, and_45_out, \output [12]);
  and and_47 (and_47_out, and_46_out, \output [13]);
  and and_48 (and_48_out, and_47_out, \output [14]);
  or or_1 (or_1_out, and_1_out, and_2_out);
  or or_2 (or_2_out, and_1_out, and_3_out);
  or or_3 (or_3_out, and_5_out, and_4_out);
  or or_4 (or_4_out, and_5_out, and_6_out);
  or or_5 (or_5_out, and_8_out, and_7_out);
  or or_6 (or_6_out, and_8_out, and_9_out);
  or or_7 (or_7_out, and_36_out, and_10_out);
  or or_8 (or_8_out, and_36_out, and_11_out);
  or or_9 (or_9_out, and_37_out, and_12_out);
  or or_10 (or_10_out, and_37_out, and_13_out);
  or or_11 (or_11_out, and_38_out, and_14_out);
  or or_12 (or_12_out, and_38_out, and_15_out);
  or or_13 (or_13_out, and_39_out, and_16_out);
  or or_14 (or_14_out, and_39_out, and_17_out);
  or or_15 (or_15_out, and_40_out, and_18_out);
  or or_16 (or_16_out, and_40_out, and_19_out);
  or or_17 (or_17_out, and_41_out, and_20_out);
  or or_18 (or_18_out, and_41_out, and_21_out);
  or or_19 (or_19_out, and_42_out, and_22_out);
  or or_20 (or_20_out, and_42_out, and_23_out);
  or or_21 (or_21_out, and_43_out, and_24_out);
  or or_22 (or_22_out, and_43_out, and_25_out);
  or or_23 (or_23_out, and_44_out, and_26_out);
  or or_24 (or_24_out, and_44_out, and_27_out);
  or or_25 (or_25_out, and_45_out, and_28_out);
  or or_26 (or_26_out, and_45_out, and_29_out);
  or or_27 (or_27_out, and_46_out, and_30_out);
  or or_28 (or_28_out, and_46_out, and_31_out);
  or or_29 (or_29_out, and_47_out, and_32_out);
  or or_30 (or_30_out, and_47_out, and_33_out);
  or or_31 (or_31_out, and_48_out, and_34_out);
  or or_32 (or_32_out, and_48_out, and_35_out);
  J_K_Flip_Flop j_k_ff_1 (
    .J(or_1_out), .clk(CLOCK), .K(or_2_out), .Q(\output [0]), .reset(CLR));  // open: Qn, preset, en
  J_K_Flip_Flop j_k_ff_2 (
    .J(or_3_out), .clk(CLOCK), .K(or_4_out), .Q(\output [1]), .reset(CLR));  // open: Qn, preset, en
  J_K_Flip_Flop j_k_ff_3 (
    .J(or_5_out), .clk(CLOCK), .K(or_6_out), .Q(\output [2]), .reset(CLR));  // open: Qn, preset, en
  J_K_Flip_Flop j_k_ff_4 (
    .J(or_7_out), .clk(CLOCK), .K(or_8_out), .Q(\output [3]), .reset(CLR));  // open: Qn, preset, en
  J_K_Flip_Flop j_k_ff_5 (
    .J(or_9_out), .clk(CLOCK), .K(or_10_out), .Q(\output [4]), .reset(CLR));  // open: Qn, preset, en
  J_K_Flip_Flop j_k_ff_6 (
    .J(or_11_out), .clk(CLOCK), .K(or_12_out), .Q(\output [5]), .reset(CLR));  // open: Qn, preset, en
  J_K_Flip_Flop j_k_ff_7 (
    .J(or_13_out), .clk(CLOCK), .K(or_14_out), .Q(\output [6]), .reset(CLR));  // open: Qn, preset, en
  J_K_Flip_Flop j_k_ff_8 (
    .J(or_15_out), .clk(CLOCK), .K(or_16_out), .Q(\output [7]), .reset(CLR));  // open: Qn, preset, en
  J_K_Flip_Flop j_k_ff_9 (
    .J(or_17_out), .clk(CLOCK), .K(or_18_out), .Q(\output [8]), .reset(CLR));  // open: Qn, preset, en
  J_K_Flip_Flop j_k_ff_10 (
    .J(or_19_out), .clk(CLOCK), .K(or_20_out), .Q(\output [9]), .reset(CLR));  // open: Qn, preset, en
  J_K_Flip_Flop j_k_ff_11 (
    .J(or_21_out), .clk(CLOCK), .K(or_22_out), .Q(\output [10]), .reset(CLR));  // open: Qn, preset, en
  J_K_Flip_Flop j_k_ff_12 (
    .J(or_23_out), .clk(CLOCK), .K(or_24_out), .Q(\output [11]), .reset(CLR));  // open: Qn, preset, en
  J_K_Flip_Flop j_k_ff_13 (
    .J(or_25_out), .clk(CLOCK), .K(or_26_out), .Q(\output [12]), .reset(CLR));  // open: Qn, preset, en
  J_K_Flip_Flop j_k_ff_14 (
    .J(or_27_out), .clk(CLOCK), .K(or_28_out), .Q(\output [13]), .reset(CLR));  // open: Qn, preset, en
  J_K_Flip_Flop j_k_ff_15 (
    .J(or_29_out), .clk(CLOCK), .K(or_30_out), .Q(\output [14]), .reset(CLR));  // open: Qn, preset, en
  J_K_Flip_Flop j_k_ff_16 (
    .J(or_31_out), .clk(CLOCK), .K(or_32_out), .Q(\output [15]), .reset(CLR));  // open: Qn, preset, en
endmodule
