// Logisim project 4bitSC.circ as structural Verilog: 1 circuit, main circuit main
module main (
  input  CLOCK,
  input  CLR,
  output [15:0] OUTPUT
);

  wire and_1_out, and_2_out, and_3_out, and_4_out, and_5_out, and_6_out, and_7_out, and_8_out, and_9_out,
       and_10_out, and_11_out, and_12_out, not_1_out, not_2_out, not_3_out, not_4_out, not_5_out, or_1_out,
       or_2_out, or_3_out, or_4_out, or_5_out, or_6_out, or_7_out, or_8_out;
  wire [3:0] j_k_ff_1_q;

  not not_1 (not_1_out, 1'b0);
  not not_2 (not_2_out, 1'b0);
  not not_3 (not_3_out, 1'b0);
  not not_4 (not_4_out, 1'b0);
  not not_5 (not_5_out, 1'b0);
  and and_1 (and_1_out, not_1_out, 1'b1);
  and and_2 (and_2_out, 1'b0, 1'b0);
  and and_3 (and_3_out, 1'b0, not_2_out);
  and and_4 (and_4_out, 1'b0, 1'b0);
  and and_5 (and_5_out, and_1_out, j_k_ff_1_q[0]);
  and and_6 (and_6_out, 1'b0, not_3_out);
  and and_7 (and_7_out, 1'b0, 1'b0);
  and and_8 (and_8_out, and_5_out, j_k_ff_1_q[1]);
  and and_9 (and_9_out, 1'b0, not_4_out);
  and and_10 (and_10_out, 1'b0, 1'b0);
  and and_11 (and_11_out, and_8_out, j_k_ff_1_q[2]);
  and and_12 (and_12_out, 1'b0, not_5_out);
  or or_1 (or_1_out, and_1_out, and_2_out);
  or or_2 (or_2_out, and_1_out, and_3_out);
  or or_3 (or_3_out, and_5_out, and_4_out);
  or or_4 (or_4_out, and_5_out, and_6_out);
  or or_5 (or_5_out, and_8_out, and_7_out);
  or or_6 (or_6_out, and_8_out, and_9_out);
  or or_7 (or_7_out, and_11_out, and_10_out);
  or or_8 (or_8_out, and_11_out, and_12_out);
  J_K_Flip_Flop j_k_ff_1 (
    .J(or_1_out), .clk(CLOCK), .K(or_2_out), .Q(j_k_ff_1_q[0]), .reset(CLR));  // open: Qn, preset, en
  J_K_Flip_Flop j_k_ff_2 (
    .J(or_3_out), .clk(CLOCK), .K(or_4_out), .Q(j_k_ff_1_q[1]), .reset(CLR));  // open: Qn, preset, en
  J_K_Flip_Flop j_k_ff_3 (
    .J(or_5_out), .clk(CLOCK), .K(or_6_out), .Q(j_k_ff_1_q[2]), .reset(CLR));  // open: Qn, preset, en
  J_K_Flip_Flop j_k_ff_4 (
    .J(or_7_out), .clk(CLOCK), .K(or_8_out), .Q(j_k_ff_1_q[3]), .reset(CLR));  // open: Qn, preset, en
  Decoder #(.select(4), .enable("false")) decoder_1 (
    .out1(OUTPUT[0]), .out2(OUTPUT[1]), .out3(OUTPUT[2]), .out4(OUTPUT[3]), .out5(OUTPUT[4]),
    .out6(OUTPUT[5]), .out7(OUTPUT[6]), .out8(OUTPUT[7]), .out9(OUTPUT[8]), .out10(OUTPUT[9]),
    .out11(OUTPUT[10]), .out12(OUTPUT[11]), .out13(OUTPUT[12]), .out14(OUTPUT[13]), .out15(OUTPUT[14]),
    .sel(j_k_ff_1_q));  // open: out0

  assign OUTPUT[15] = 1'b0;

  // Notes on the sheet:
  //   load
endmodule
