// Logisim project AR.circ as structural Verilog: 1 circuit, main circuit main
module main (
  input  D7_prime,
  input  I,
  input  T3,
  input  T2,
  input  T0,
  input  D5,
  input  T4,
  output load_AR,
  output INC_AR
);

  wire and_1_out;

  and and_1 (and_1_out, D7_prime, I, T3);
  and and_2 (INC_AR, D5, T4);
  or or_1 (load_AR, and_1_out, T2, T0);
endmodule
