// Logisim project BUS .circ as structural Verilog: 1 circuit, main circuit main
module main (
  input  D0,
  input  D1,
  input  D2,
  input  D3,
  input  D4,
  input  D5,
  input  D6,
  input  D7,
  input  T0,
  input  T1,
  input  T2,
  input  T3,
  input  T4,
  input  T5,
  input  T6,
  input  T7,
  input  I,
  input  P,
  input  B10,
  output S2,
  output S1,
  output S0
);

  wire and_1_out, and_2_out, and_3_out, and_4_out, and_5_out, and_6_out, and_7_out, and_8_out, and_9_out,
       and_10_out, and_11_out, and_12_out, not_1_out, or_1_out, or_2_out, or_3_out, or_4_out, or_6_out;

  and and_1 (and_1_out, P, B10);
  and and_2 (and_2_out, D4, T4);
  and and_3 (and_3_out, D5, T5);
  and and_4 (and_4_out, T4, D5);
  and and_5 (and_5_out, D2, T5);
  and and_6 (and_6_out, D6, T6);
  and and_7 (and_7_out, D3, T4);
  not not_1 (not_1_out, D7);
  or or_1 (or_1_out, and_2_out, and_3_out);
  or or_2 (or_2_out, and_4_out, T0);
  or or_3 (or_3_out, and_5_out, and_6_out);
  or or_4 (or_4_out, and_7_out, and_1_out);
  and and_8 (and_8_out, not_1_out, T3, I);
  and and_9 (and_9_out, D0, T4);
  and and_10 (and_10_out, D1, T4);
  and and_11 (and_11_out, D2, T4);
  and and_12 (and_12_out, D6, T4);
  or or_5 (S2, or_4_out, T2, 1'b0, or_6_out);
  or or_6 (or_6_out, T1, and_8_out, and_9_out, and_10_out, and_11_out, and_12_out);
  or or_7 (S1, or_2_out, or_3_out, 1'b0, or_6_out);
  or or_8 (S0, or_1_out, or_3_out, T2, or_6_out);

  // Notes on the sheet:
  //   X1
  //   X2
  //   X3
  //   X4
  //   X5
  //   X6
  //   X7
endmodule
