// Logisim project BUS(main).circ as structural Verilog: 1 circuit, main circuit main
module main (
  input  [11:0] AR,
  input  [11:0] PC,
  input  [15:0] DR,
  input  [15:0] AC,
  input  S2,
  input  S1,
  input  S0,
  input  [15:0] IR,
  input  [15:0] TR,
  input  [15:0] Main_MR,
  output [15:0] BUS_OUTPUT
);

  wire [15:0] bit_extender_1_out, bit_extender_2_out;

  assign bit_extender_1_out = {{4{1'b0}}, AR};  // Bit_Extender bit_extender_1
  assign bit_extender_2_out = {{4{1'b0}}, PC};  // Bit_Extender bit_extender_2
  Multiplexer #(.select(3), .width(16), .enable("false")) multiplexer_1 (
    .in0({16{1'b0}}), .in1(bit_extender_1_out), .in2(bit_extender_2_out), .in3(DR), .in4(AC), .in5(IR),
    .in6(TR), .in7(Main_MR), .out(BUS_OUTPUT), .sel({S2, S1, S0}));
endmodule
