// Logisim project Computetr1.circ as structural Verilog: 1 circuit, main circuit main
module main (
  input  in_1,
  input  in_2,
  input  [15:0] TR_OUT,
  input  [15:0] TR_OUT_2,
  input  [7:0] in_5,
  output [15:0] out_6,
  output out_7,
  output [15:0] BUS_OUTPUT,
  output [11:0] AR_OUT,
  output [11:0] PC_OUT,
  output [15:0] DR_OUT,
  output [15:0] DR_OUT_2,
  output [15:0] SC_OUT,
  output [7:0] out_14
);

  wire and_1_out, and_2_out, clock_1_out, CPU_bus_s0, CPU_bus_s1, CPU_bus_s2, CPU_clr_sc, CPU_inc_ar,
       CPU_inc_dr, CPU_inc_pc, CPU_load_ar, CPU_load_dr, CPU_load_pc, CPU_p, CPU_r_2, decoder_1_out0,
       decoder_1_out1, decoder_1_out2, decoder_1_out3, decoder_1_out4, decoder_1_out5, decoder_1_out6,
       decoder_1_out7, j_k_ff_1_q, j_k_ff_2_q, not_1_out, not_2_out, not_3_out, RAM_CONT_ram_cont;
  wire [7:0] bit_extender_1_out, INPR_inpr_out;
  wire [11:0] bit_extender_2_out;
  wire [15:0] ram_1_data;

  _4bitSC_main SC (.CLOCK(clock_1_out), .CLR(CPU_clr_sc), .OUTPUT(SC_OUT));
  and and_1 (and_1_out, DR_OUT_2[11], CPU_p);
  and and_2 (and_2_out, CPU_p, DR_OUT_2[10]);
  not not_1 (not_1_out, 1'b1);
  not not_2 (not_2_out, and_2_out);
  cpu_main CPU (
    .T7(SC_OUT[7]), .D0(decoder_1_out0), .D1(decoder_1_out1), .D2(decoder_1_out2), .D3(decoder_1_out3),
    .D4(decoder_1_out4), .D5(decoder_1_out5), .D6(decoder_1_out6), .D7(decoder_1_out7), .T0(SC_OUT[0]),
    .T1(SC_OUT[1]), .T2(SC_OUT[2]), .T3(SC_OUT[3]), .T4(SC_OUT[4]), .T5(SC_OUT[5]), .T6(SC_OUT[6]),
    .R(clock_1_out), .Clock(clock_1_out), .AC_15(out_6[15]), .DR_OUt(DR_OUT), .AC_OUT(out_6),
    .B0(DR_OUT_2[0]), .B1(DR_OUT_2[1]), .B2(DR_OUT_2[2]), .B3(DR_OUT_2[3]), .B4(DR_OUT_2[4]), .E(out_7),
    .B5(DR_OUT_2[5]), .B6(DR_OUT_2[6]), .FGI(j_k_ff_2_q), .FGO(j_k_ff_1_q), .B7(DR_OUT_2[7]),
    .B8(DR_OUT_2[8]), .B9(DR_OUT_2[9]), .B10(DR_OUT_2[10]), .IR_15(DR_OUT_2[15]), .load_AR(CPU_load_ar),
    .INC_AR(CPU_inc_ar), .load_DR(CPU_load_dr), .INC_DR(CPU_inc_dr), .CLR_SC(CPU_clr_sc),
    .bus_s2(CPU_bus_s2), .bus_s1(CPU_bus_s1), .bus_S0(CPU_bus_s0), .LOAD_PC(CPU_load_pc),
    .INC_PC(CPU_inc_pc), .P(CPU_p), .r_2(CPU_r_2));  // open: J_S_F_F, K_S_F_F
  J_K_Flip_Flop j_k_ff_1 (
    .J(not_2_out), .clk(clock_1_out), .K(and_2_out), .Q(j_k_ff_1_q));  // open: Qn, preset, en, reset
  not not_3 (not_3_out, RAM_CONT_ram_cont);
  J_K_Flip_Flop j_k_ff_2 (
    .J(1'b1), .clk(clock_1_out), .K(not_1_out), .Q(j_k_ff_2_q), .reset(and_1_out));  // open: Qn, preset, en
  RAM #(.addrWidth(12), .dataWidth(16)) ram_1 (
    .addr(AR_OUT), .data(ram_1_data), .sel(1'b1), .clk(clock_1_out), .ld(not_3_out));  // open: clr
  Decoder #(.select(3)) decoder_1 (
    .out0(decoder_1_out0), .out1(decoder_1_out1), .out2(decoder_1_out2), .out3(decoder_1_out3),
    .out4(decoder_1_out4), .out5(decoder_1_out5), .out6(decoder_1_out6), .out7(decoder_1_out7),
    .sel(DR_OUT_2[14:12]));  // open: en
  INPR_main INPR (.INPR_IN(in_5), .CLOCK(clock_1_out), .INPR_OUT(INPR_inpr_out));
  assign ram_1_data = RAM_CONT_ram_cont ? BUS_OUTPUT : 16'bz;  // Controlled_Buffer controlled_buffer_1
  RAM_main RAM_CONT (
    .D3(decoder_1_out3), .T4(SC_OUT[4]), .D5(decoder_1_out5), .T4_2(SC_OUT[4]), .D6(decoder_1_out6),
    .T6(SC_OUT[6]), .RAM_CONT(RAM_CONT_ram_cont));
  Clock clock_1 (.out(clock_1_out));
  OUTR_main OUTER (.P(CPU_p), .B10(DR_OUT_2[10]), .INPUT(bit_extender_1_out), .CLOCK(clock_1_out), .OUTPUT(out_14));
  Bit_Extender #(.in_width(16), .out_width(8)) bit_extender_1 (.in(BUS_OUTPUT), .out(bit_extender_1_out));
  r12_LD_INR_CLR__AR_PC__main AR (
    .LD(CPU_load_ar), .INC(CPU_inc_ar), .INPUT(bit_extender_2_out), .CLOCK(clock_1_out), .OUTPUT(AR_OUT));  // open: CLR
  r12_LD_INR_CLR__AR_PC__main PC (
    .LD(CPU_load_pc), .INC(CPU_inc_pc), .INPUT(bit_extender_2_out), .CLOCK(clock_1_out), .OUTPUT(PC_OUT));  // open: CLR
  _16bit_reg_main DR (
    .load(CPU_load_dr), .INC(CPU_inc_dr), .\input (BUS_OUTPUT), .CLOCK(clock_1_out), .\output (DR_OUT));  // open: CLR
  IR_main main_1 (.T1(SC_OUT[1]), .\input (BUS_OUTPUT), .CLOCK(clock_1_out), .\output (DR_OUT_2));
  TR_main main_2 (.LD(in_2), .INPUT(TR_OUT), .OUTPUT(TR_OUT_2), .CLOCK(clock_1_out));
  adder_AC_bus_main AC (
    .AC_out(out_6), .D0(decoder_1_out0), .T5(SC_OUT[5]), .D1(decoder_1_out1), .D2(decoder_1_out2), .p(CPU_p),
    .b11(DR_OUT_2[11]), .r(CPU_r_2), .b9(DR_OUT_2[9]), .b7(DR_OUT_2[7]), .b6(DR_OUT_2[6]), .b5(DR_OUT_2[5]),
    .b11_2(DR_OUT_2[11]), .r_2(CPU_r_2), .B8(DR_OUT_2[8]), .r_3(CPU_r_2), .B10(DR_OUT_2[10]),
    .from_DR(DR_OUT), .E_CLR(in_1), .from_INPR(INPR_inpr_out), .CLOCK(clock_1_out), .E_IN(in_1), .E_OUT(out_7));
  Bit_Extender #(.in_width(16), .out_width(12)) bit_extender_2 (.in(BUS_OUTPUT), .out(bit_extender_2_out));
  BUS_main__main BUS (
    .AR(AR_OUT), .PC(PC_OUT), .DR(DR_OUT), .AC(out_6), .IR(DR_OUT_2), .TR(TR_OUT_2), .Main_MR(ram_1_data),
    .S2(CPU_bus_s2), .S1(CPU_bus_s1), .S0(CPU_bus_s0), .BUS_OUTPUT(BUS_OUTPUT));
endmodule
