// Logisim project DR.circ as structural Verilog: 1 circuit, main circuit main
module main (
  input  T4,
  input  D0,
  input  D1,
  input  D2,
  input  D6,
  input  T5,
  output LOAd_DR,
  output INC_DR
);

  wire and_1_out, and_2_out, and_3_out, and_4_out;

  and and_1 (and_1_out, T4, D0);
  and and_2 (and_2_out, T4, D1);
  and and_3 (and_3_out, T4, D2);
  and and_4 (and_4_out, T4, D6);
  and and_5 (INC_DR, D6, T5);
  or or_1 (LOAd_DR, and_1_out, and_2_out, and_3_out, and_4_out);
endmodule
