// Logisim project I(FF).circ as structural Verilog: 1 circuit, main circuit main
module main (
  input  IR_15,
  input  T2,
  input  CLOCK,
  output I_OUT
);

  wire not_1_out;

  not not_1 (not_1_out, IR_15);
  J_K_Flip_Flop j_k_ff_1 (.J(IR_15), .clk(CLOCK), .K(not_1_out), .Q(I_OUT), .en(T2));  // open: Qn, preset, reset
endmodule
