// Logisim project IEN.circ as structural Verilog: 1 circuit, main circuit main
module main (
  input  P,
  input  B7,
  input  R,
  input  T2,
  input  P_2,
  input  Clock,
  input  B6,
  output IEN_out
);

  wire and_1_out, and_2_out, and_3_out, or_1_out;

  and and_1 (and_1_out, R, T2);
  and and_2 (and_2_out, P_2, B6);
  or or_1 (or_1_out, and_1_out, and_2_out);
  and and_3 (and_3_out, P, B7);
  J_K_Flip_Flop j_k_ff_1 (.J(and_3_out), .clk(Clock), .K(or_1_out), .Q(IEN_out));  // open: Qn, preset, en, reset
endmodule
