// Logisim project INPR.circ as structural Verilog: 1 circuit, main circuit main
module main (
  input  [7:0] INPR_IN,
  input  CLOCK,
  output [7:0] INPR_OUT
);

  wire not_1_out, not_2_out, not_3_out, not_4_out, not_5_out, not_6_out, not_7_out, not_8_out;

  not not_1 (not_1_out, INPR_IN[0]);
  not not_2 (not_2_out, INPR_IN[1]);
  not not_3 (not_3_out, INPR_IN[2]);
  not not_4 (not_4_out, INPR_IN[3]);
  not not_5 (not_5_out, INPR_IN[4]);
  not not_6 (not_6_out, INPR_IN[5]);
  not not_7 (not_7_out, INPR_IN[6]);
  not not_8 (not_8_out, INPR_IN[7]);
  J_K_Flip_Flop j_k_ff_1 (.J(INPR_IN[0]), .clk(CLOCK), .K(not_1_out), .Q(INPR_OUT[0]));  // open: Qn, preset, en, reset
  J_K_Flip_Flop j_k_ff_2 (.J(INPR_IN[1]), .clk(CLOCK), .K(not_2_out), .Q(INPR_OUT[1]));  // open: Qn, preset, en, reset
  J_K_Flip_Flop j_k_ff_3 (.J(INPR_IN[2]), .clk(CLOCK), .K(not_3_out), .Q(INPR_OUT[2]));  // open: Qn, preset, en, reset
  J_K_Flip_Flop j_k_ff_4 (.J(INPR_IN[3]), .clk(CLOCK), .K(not_4_out), .Q(INPR_OUT[3]));  // open: Qn, preset, en, reset
  J_K_Flip_Flop j_k_ff_5 (.J(INPR_IN[4]), .clk(CLOCK), .K(not_5_out), .Q(INPR_OUT[4]));  // open: Qn, preset, en, reset
  J_K_Flip_Flop j_k_ff_6 (.J(INPR_IN[5]), .clk(CLOCK), .K(not_6_out), .Q(INPR_OUT[5]));  // open: Qn, preset, en, reset
  J_K_Flip_Flop j_k_ff_7 (.J(INPR_IN[6]), .clk(CLOCK), .K(not_7_out), .Q(INPR_OUT[6]));  // open: Qn, preset, en, reset
  J_K_Flip_Flop j_k_ff_8 (.J(INPR_IN[7]), .clk(CLOCK), .K(not_8_out), .Q(INPR_OUT[7]));  // open: Qn, preset, en, reset
endmodule
