// Logisim project IR.circ as structural Verilog: 1 circuit, main circuit main
module main (
  input  T1,
  input  [15:0] \input ,
  input  CLOCK,
  output [15:0] \output 
);

  wire and_1_out, and_2_out, and_3_out, and_4_out, and_5_out, and_6_out, and_7_out, and_8_out, and_9_out,
       and_10_out, and_11_out, and_12_out, and_13_out, and_14_out, and_15_out, and_16_out, and_17_out,
       and_18_out, and_19_out, and_20_out, and_21_out, and_22_out, and_23_out, and_24_out, and_25_out,
       and_26_out, and_27_out, and_28_out, and_29_out, and_30_out, and_31_out, and_32_out, not_1_out,
       not_2_out, not_3_out, not_4_out, not_5_out, not_6_out, not_7_out, not_8_out, not_9_out, not_10_out,
       not_11_out, not_12_out, not_13_out, not_14_out, not_15_out, not_16_out, undriven, undriven_2,
       undriven_3, undriven_4, undriven_5, undriven_6, undriven_7, undriven_8, undriven_9, undriven_10,
       undriven_11, undriven_12, undriven_13, undriven_14, undriven_15, undriven_16;

  not not_1 (not_1_out, \input [0]);
  not not_2 (not_2_out, \input [1]);
  not not_3 (not_3_out, \input [2]);
  not not_4 (not_4_out, \input [3]);
  not not_5 (not_5_out, \input [4]);
  not not_6 (not_6_out, \input [5]);
  not not_7 (not_7_out, \input [6]);
  not not_8 (not_8_out, \input [7]);
  not not_9 (not_9_out, \input [8]);
  not not_10 (not_10_out, \input [9]);
  not not_11 (not_11_out, \input [10]);
  not not_12 (not_12_out, \input [11]);
  not not_13 (not_13_out, \input [12]);
  not not_14 (not_14_out, \input [13]);
  not not_15 (not_15_out, \input [14]);
  not not_16 (not_16_out, \input [15]);
  and and_1 (and_1_out, T1, \input [0]);
  and and_2 (and_2_out, T1, not_1_out);
  and and_3 (and_3_out, T1, \input [1]);
  and and_4 (and_4_out, T1, not_2_out);
  and and_5 (and_5_out, T1, \input [2]);
  and and_6 (and_6_out, T1, not_3_out);
  and and_7 (and_7_out, T1, \input [3]);
  and and_8 (and_8_out, T1, not_4_out);
  and and_9 (and_9_out, T1, \input [4]);
  and and_10 (and_10_out, T1, not_5_out);
  and and_11 (and_11_out, T1, \input [5]);
  and and_12 (and_12_out, T1, not_6_out);
  and and_13 (and_13_out, T1, \input [6]);
  and and_14 (and_14_out, T1, not_7_out);
  and and_15 (and_15_out, T1, \input [7]);
  and and_16 (and_16_out, T1, not_8_out);
  and and_17 (and_17_out, T1, \input [8]);
  and and_18 (and_18_out, T1, not_9_out);
  and and_19 (and_19_out, T1, \input [9]);
  and and_20 (and_20_out, T1, not_10_out);
  and and_21 (and_21_out, T1, \input [10]);
  and and_22 (and_22_out, T1, not_11_out);
  and and_23 (and_23_out, T1, \input [11]);
  and and_24 (and_24_out, T1, not_12_out);
  and and_25 (and_25_out, T1, \input [12]);
  and and_26 (and_26_out, T1, not_13_out);
  and and_27 (and_27_out, T1, \input [13]);
  and and_28 (and_28_out, T1, not_14_out);
  and and_29 (and_29_out, T1, \input [14]);
  and and_30 (and_30_out, T1, not_15_out);
  and and_31 (and_31_out, T1, \input [15]);
  and and_32 (and_32_out, T1, not_16_out);
  J_K_Flip_Flop j_k_ff_1 (
    .J(and_1_out), .clk(CLOCK), .K(and_2_out), .Q(\output [0]), .reset(undriven));  // open: Qn, preset, en
  J_K_Flip_Flop j_k_ff_2 (
    .J(and_3_out), .clk(CLOCK), .K(and_4_out), .Q(\output [1]), .reset(undriven_2));  // open: Qn, preset, en
  J_K_Flip_Flop j_k_ff_3 (
    .J(and_5_out), .clk(CLOCK), .K(and_6_out), .Q(\output [2]), .reset(undriven_3));  // open: Qn, preset, en
  J_K_Flip_Flop j_k_ff_4 (
    .J(and_7_out), .clk(CLOCK), .K(and_8_out), .Q(\output [3]), .reset(undriven_4));  // open: Qn, preset, en
  J_K_Flip_Flop j_k_ff_5 (
    .J(and_9_out), .clk(CLOCK), .K(and_10_out), .Q(\output [4]), .reset(undriven_5));  // open: Qn, preset, en
  J_K_Flip_Flop j_k_ff_6 (
    .J(and_11_out), .clk(CLOCK), .K(and_12_out), .Q(\output [5]), .reset(undriven_6));  // open: Qn, preset, en
  J_K_Flip_Flop j_k_ff_7 (
    .J(and_13_out), .clk(CLOCK), .K(and_14_out), .Q(\output [6]), .reset(undriven_7));  // open: Qn, preset, en
  J_K_Flip_Flop j_k_ff_8 (
    .J(and_15_out), .clk(CLOCK), .K(and_16_out), .Q(\output [7]), .reset(undriven_8));  // open: Qn, preset, en
  J_K_Flip_Flop j_k_ff_9 (
    .J(and_17_out), .clk(CLOCK), .K(and_18_out), .Q(\output [8]), .reset(undriven_9));  // open: Qn, preset, en
  J_K_Flip_Flop j_k_ff_10 (
    .J(and_19_out), .clk(CLOCK), .K(and_20_out), .Q(\output [9]), .reset(undriven_10));  // open: Qn, preset, en
  J_K_Flip_Flop j_k_ff_11 (
    .J(and_21_out), .clk(CLOCK), .K(and_22_out), .Q(\output [10]), .reset(undriven_11));  // open: Qn, preset, en
  J_K_Flip_Flop j_k_ff_12 (
    .J(and_23_out), .clk(CLOCK), .K(and_24_out), .Q(\output [11]), .reset(undriven_12));  // open: Qn, preset, en
  J_K_Flip_Flop j_k_ff_13 (
    .J(and_25_out), .clk(CLOCK), .K(and_26_out), .Q(\output [12]), .reset(undriven_13));  // open: Qn, preset, en
  J_K_Flip_Flop j_k_ff_14 (
    .J(and_27_out), .clk(CLOCK), .K(and_28_out), .Q(\output [13]), .reset(undriven_14));  // open: Qn, preset, en
  J_K_Flip_Flop j_k_ff_15 (
    .J(and_29_out), .clk(CLOCK), .K(and_30_out), .Q(\output [14]), .reset(undriven_15));  // open: Qn, preset, en
  J_K_Flip_Flop j_k_ff_16 (
    .J(and_31_out), .clk(CLOCK), .K(and_32_out), .Q(\output [15]), .reset(undriven_16));  // open: Qn, preset, en
endmodule
