// Logisim project OUTR.circ as structural Verilog: 1 circuit, main circuit main
module main (
  input  P,
  input  B10,
  input  [7:0] INPUT,
  input  CLOCK,
  output [7:0] OUTPUT
);

  wire and_1_out, and_2_out, and_3_out, and_4_out, and_5_out, and_6_out, and_7_out, and_8_out, and_9_out,
       and_10_out, and_11_out, and_12_out, and_13_out, and_14_out, and_15_out, and_16_out, and_17_out,
       not_1_out, not_2_out, not_3_out, not_4_out, not_5_out, not_6_out, not_7_out, not_8_out;

  and and_1 (and_1_out, P, B10);
  not not_1 (not_1_out, INPUT[0]);
  not not_2 (not_2_out, INPUT[1]);
  not not_3 (not_3_out, INPUT[2]);
  not not_4 (not_4_out, INPUT[3]);
  not not_5 (not_5_out, INPUT[4]);
  not not_6 (not_6_out, INPUT[5]);
  not not_7 (not_7_out, INPUT[6]);
  not not_8 (not_8_out, INPUT[7]);
  and and_2 (and_2_out, and_1_out, INPUT[0]);
  and and_3 (and_3_out, and_1_out, not_1_out);
  and and_4 (and_4_out, and_1_out, INPUT[1]);
  and and_5 (and_5_out, and_1_out, not_2_out);
  and and_6 (and_6_out, and_1_out, INPUT[2]);
  and and_7 (and_7_out, and_1_out, not_3_out);
  and and_8 (and_8_out, and_1_out, INPUT[3]);
  and and_9 (and_9_out, and_1_out, not_4_out);
  and and_10 (and_10_out, and_1_out, INPUT[4]);
  and and_11 (and_11_out, and_1_out, not_5_out);
  and and_12 (and_12_out, and_1_out, INPUT[5]);
  and and_13 (and_13_out, and_1_out, not_6_out);
  and and_14 (and_14_out, and_1_out, INPUT[6]);
  and and_15 (and_15_out, and_1_out, not_7_out);
  and and_16 (and_16_out, and_1_out, INPUT[7]);
  and and_17 (and_17_out, and_1_out, not_8_out);
  J_K_Flip_Flop j_k_ff_1 (.J(and_2_out), .clk(CLOCK), .K(and_3_out), .Q(OUTPUT[0]));  // open: Qn, preset, en, reset
  J_K_Flip_Flop j_k_ff_2 (.J(and_4_out), .clk(CLOCK), .K(and_5_out), .Q(OUTPUT[1]));  // open: Qn, preset, en, reset
  J_K_Flip_Flop j_k_ff_3 (.J(and_6_out), .clk(CLOCK), .K(and_7_out), .Q(OUTPUT[2]));  // open: Qn, preset, en, reset
  J_K_Flip_Flop j_k_ff_4 (.J(and_8_out), .clk(CLOCK), .K(and_9_out), .Q(OUTPUT[3]));  // open: Qn, preset, en, reset
  J_K_Flip_Flop j_k_ff_5 (.J(and_10_out), .clk(CLOCK), .K(and_11_out), .Q(OUTPUT[4]));  // open: Qn, preset, en, reset
  J_K_Flip_Flop j_k_ff_6 (.J(and_12_out), .clk(CLOCK), .K(and_13_out), .Q(OUTPUT[5]));  // open: Qn, preset, en, reset
  J_K_Flip_Flop j_k_ff_7 (.J(and_14_out), .clk(CLOCK), .K(and_15_out), .Q(OUTPUT[6]));  // open: Qn, preset, en, reset
  J_K_Flip_Flop j_k_ff_8 (.J(and_16_out), .clk(CLOCK), .K(and_17_out), .Q(OUTPUT[7]));  // open: Qn, preset, en, reset

  // Notes on the sheet:
  //   OUTR
endmodule
