// Logisim project RAM.circ as structural Verilog: 1 circuit, main circuit main
module main (
  input  D3,
  input  T4,
  input  D5,
  input  T4_2,
  input  D6,
  input  T6,
  output RAM_CONT
);

  wire and_1_out, and_2_out, and_3_out;

  and and_1 (and_1_out, D3, T4);
  and and_2 (and_2_out, D5, T4_2);
  and and_3 (and_3_out, D6, T6);
  or or_1 (RAM_CONT, and_1_out, and_2_out, and_3_out);
endmodule
