// Logisim project S(FF).circ as structural Verilog: 1 circuit, main circuit main
module main (
  input  r,
  input  B0,
  output J_S_F_F,
  output K_S_F_F
);

  wire and_1_out;

  and and_1 (and_1_out, r, B0);
  not not_1 (J_S_F_F, and_1_out);
  not not_2 (K_S_F_F, J_S_F_F);
endmodule
