// Logisim project TR.circ as structural Verilog: 1 circuit, main circuit main
module main (
  input  LD,
  input  [15:0] INPUT,
  input  CLOCK,
  output [15:0] OUTPUT
);

  _16bit_reg_main main_1 (.load(LD), .INC(1'b0), .\input (INPUT), .CLOCK(CLOCK), .CLR(1'b0), .\output (OUTPUT));
endmodule
