// Logisim project add&lc.circ as structural Verilog: 1 circuit, main circuit main
module main (
  input  _0inpr,
  input  _1inpr,
  input  _2inpr,
  input  _3inpr,
  input  AND_prime,
  input  _0,
  input  _0AC,
  input  _1AC,
  input  _2AC,
  input  _3AC,
  input  ADD_prime,
  input  DR_prime,
  input  _0DR,
  input  _1DR,
  input  _2dr,
  input  _3DR,
  input  INPR_prime,
  input  COM_prime,
  input  SHR_prime,
  input  _4inpr,
  input  _5inpr,
  input  _6inpr,
  input  _7inpr,
  input  SHL_prime,
  input  _4AC,
  input  _5AC,
  input  _6AC,
  input  _7AC,
  input  _4DR,
  input  _5DR,
  input  _6DR,
  input  _7DR,
  input  _8AC,
  input  _9AC,
  input  _10AC,
  input  _11AC,
  input  _8DR,
  input  _9DR,
  input  _10DR,
  input  _11DR,
  input  FROM_E,
  input  _12AC,
  input  _13AC,
  input  _14AC,
  input  _15AC,
  input  _12DR,
  input  _13DR,
  input  _14DR,
  input  _15DR,
  output _2AC_prime,
  output _3AC_prime,
  output _0AC_prime,
  output _1AC_prime,
  output _7AC_prime,
  output _4AC_prime,
  output _5AC_prime,
  output _6AC_prime,
  output C_OUT,
  output _11AC_prime,
  output _8AC_prime,
  output _9AC_prime,
  output _10AC_prime,
  output E_IN,
  output _12AC_prime,
  output _13AC_prime,
  output _14AC_prime,
  output _15AC_prime
);

  wire ac0_cout, ac1_cout, ac2_cout, ac3_cout, ac4_cout, ac5_cout, ac6_cout, ac7_cout, ac9_cout, ac10_cout,
       ac11_cout, ac12_cout, ac13_cout, ac14_cout, and_1_out, and_2_out, main_1_cout;

  adder_lc_main ac0 (
    .AND(AND_prime), .cin(_0), .ADD(ADD_prime), .cout(ac0_cout), .DR(DR_prime), .INPR(INPR_prime),
    .com(COM_prime), .shr(SHR_prime), .i_1_ac(_1AC), .shl(SHL_prime), .i_1_ac_2(FROM_E), .iINPR(_0inpr),
    .iAC(_0AC), .iAC_2(_0AC_prime), .iDR(_0DR));
  adder_lc_main ac4 (
    .AND(AND_prime), .cin(ac3_cout), .ADD(ADD_prime), .cout(ac4_cout), .DR(DR_prime), .INPR(INPR_prime),
    .com(COM_prime), .shr(SHR_prime), .i_1_ac(_5AC), .shl(SHL_prime), .i_1_ac_2(_3AC), .iINPR(_4inpr),
    .iAC(_4AC), .iAC_2(_4AC_prime), .iDR(_4DR));
  adder_lc_main main_1 (
    .AND(AND_prime), .cin(ac7_cout), .ADD(ADD_prime), .cout(main_1_cout), .DR(DR_prime), .INPR(INPR_prime),
    .com(COM_prime), .shr(SHR_prime), .i_1_ac(_9AC), .shl(SHL_prime), .i_1_ac_2(_7AC), .iINPR(_0),
    .iAC(_8AC), .iAC_2(_8AC_prime), .iDR(_8DR));
  adder_lc_main ac12 (
    .AND(AND_prime), .cin(ac11_cout), .ADD(ADD_prime), .cout(ac12_cout), .DR(DR_prime), .INPR(INPR_prime),
    .com(COM_prime), .shr(SHR_prime), .i_1_ac(_13AC), .shl(SHL_prime), .i_1_ac_2(_11AC), .iINPR(_0),
    .iAC(_12AC), .iAC_2(_12AC_prime), .iDR(_12DR));
  and and_1 (and_1_out, _0AC, SHR_prime);
  adder_lc_main ac1 (
    .AND(AND_prime), .cin(ac0_cout), .ADD(ADD_prime), .cout(ac1_cout), .DR(DR_prime), .INPR(INPR_prime),
    .com(COM_prime), .shr(SHR_prime), .i_1_ac(_2AC), .shl(SHL_prime), .i_1_ac_2(_0AC), .iINPR(_1inpr),
    .iAC(_1AC), .iAC_2(_1AC_prime), .iDR(_1DR));
  adder_lc_main ac5 (
    .AND(AND_prime), .cin(ac4_cout), .ADD(ADD_prime), .cout(ac5_cout), .DR(DR_prime), .INPR(INPR_prime),
    .com(COM_prime), .shr(SHR_prime), .i_1_ac(_6AC), .shl(SHL_prime), .i_1_ac_2(_4AC), .iINPR(_5inpr),
    .iAC(_5AC), .iAC_2(_5AC_prime), .iDR(_5DR));
  adder_lc_main ac9 (
    .AND(AND_prime), .cin(main_1_cout), .ADD(ADD_prime), .cout(ac9_cout), .DR(DR_prime), .INPR(INPR_prime),
    .com(COM_prime), .shr(SHR_prime), .i_1_ac(_10AC), .shl(SHL_prime), .i_1_ac_2(_8AC), .iINPR(_0),
    .iAC(_9AC), .iAC_2(_9AC_prime), .iDR(_9DR));
  adder_lc_main ac13 (
    .AND(AND_prime), .cin(ac12_cout), .ADD(ADD_prime), .cout(ac13_cout), .DR(DR_prime), .INPR(INPR_prime),
    .com(COM_prime), .shr(SHR_prime), .i_1_ac(_14AC), .shl(SHL_prime), .i_1_ac_2(_12AC), .iINPR(_0),
    .iAC(_13AC), .iAC_2(_13AC_prime), .iDR(_13DR));
  adder_lc_main ac2 (
    .AND(AND_prime), .cin(ac1_cout), .ADD(ADD_prime), .cout(ac2_cout), .DR(DR_prime), .INPR(INPR_prime),
    .com(COM_prime), .shr(SHR_prime), .i_1_ac(_3AC), .shl(SHL_prime), .i_1_ac_2(_1AC), .iINPR(_2inpr),
    .iAC(_2AC), .iAC_2(_2AC_prime), .iDR(_2dr));
  adder_lc_main ac6 (
    .AND(AND_prime), .cin(ac5_cout), .ADD(ADD_prime), .cout(ac6_cout), .DR(DR_prime), .INPR(INPR_prime),
    .com(COM_prime), .shr(SHR_prime), .i_1_ac(_7AC), .shl(SHL_prime), .i_1_ac_2(_5AC), .iINPR(_6inpr),
    .iAC(_6AC), .iAC_2(_6AC_prime), .iDR(_6DR));
  adder_lc_main ac10 (
    .AND(AND_prime), .cin(ac9_cout), .ADD(ADD_prime), .cout(ac10_cout), .DR(DR_prime), .INPR(INPR_prime),
    .com(COM_prime), .shr(SHR_prime), .i_1_ac(_11AC), .shl(SHL_prime), .i_1_ac_2(_9AC), .iINPR(_0),
    .iAC(_10AC), .iAC_2(_10AC_prime), .iDR(_10DR));
  adder_lc_main ac14 (
    .AND(AND_prime), .cin(ac13_cout), .ADD(ADD_prime), .cout(ac14_cout), .DR(DR_prime), .INPR(INPR_prime),
    .com(COM_prime), .shr(SHR_prime), .i_1_ac(_15AC), .shl(SHL_prime), .i_1_ac_2(_13AC), .iINPR(_0),
    .iAC(_14AC), .iAC_2(_14AC_prime), .iDR(_14DR));
  adder_lc_main ac3 (
    .AND(AND_prime), .cin(ac2_cout), .ADD(ADD_prime), .cout(ac3_cout), .DR(DR_prime), .INPR(INPR_prime),
    .com(COM_prime), .shr(SHR_prime), .i_1_ac(_4AC), .shl(SHL_prime), .i_1_ac_2(_2AC), .iINPR(_3inpr),
    .iAC(_3AC), .iAC_2(_3AC_prime), .iDR(_3DR));
  adder_lc_main ac7 (
    .AND(AND_prime), .cin(ac6_cout), .ADD(ADD_prime), .cout(ac7_cout), .DR(DR_prime), .INPR(INPR_prime),
    .com(COM_prime), .shr(SHR_prime), .i_1_ac(_8AC), .shl(SHL_prime), .i_1_ac_2(_6AC), .iINPR(_7inpr),
    .iAC(_7AC), .iAC_2(_7AC_prime), .iDR(_7DR));
  adder_lc_main ac11 (
    .AND(AND_prime), .cin(ac10_cout), .ADD(ADD_prime), .cout(ac11_cout), .DR(DR_prime), .INPR(INPR_prime),
    .com(COM_prime), .shr(SHR_prime), .i_1_ac(_12AC), .shl(SHL_prime), .i_1_ac_2(_10AC), .iINPR(_0),
    .iAC(_11AC), .iAC_2(_11AC_prime), .iDR(_11DR));
  adder_lc_main ac15 (
    .AND(AND_prime), .cin(ac14_cout), .ADD(ADD_prime), .cout(C_OUT), .DR(DR_prime), .INPR(INPR_prime),
    .com(COM_prime), .shr(SHR_prime), .i_1_ac(FROM_E), .shl(SHL_prime), .i_1_ac_2(_14AC), .iINPR(_0),
    .iAC(_15AC), .iAC_2(_15AC_prime), .iDR(_15DR));
  and and_2 (and_2_out, _15AC, SHL_prime);
  or or_1 (E_IN, and_1_out, and_2_out);
endmodule
