// Logisim project adder&lc.circ as structural Verilog: 1 circuit, main circuit main
module main (
  input  iINPR,
  input  iAC,
  input  AND,
  input  cin,
  input  ADD,
  input  DR,
  input  INPR,
  input  iDR,
  input  com,
  input  shr,
  input  i_1_ac,
  input  shl,
  input  i_1_ac_2,
  output iAC_2,
  output cout
);

  wire adder_1_out, and_1_out, and_2_out, and_3_out, and_4_out, and_5_out, and_6_out, and_7_out, not_1_out;

  Adder #(.width(1)) adder_1 (.a(iAC), .b(iDR), .out(adder_1_out), .cin(cin), .cout(cout));
  not not_1 (not_1_out, iAC);
  and and_1 (and_1_out, AND, iAC, iDR);
  and and_2 (and_2_out, ADD, adder_1_out);
  and and_3 (and_3_out, iDR, DR);
  and and_4 (and_4_out, INPR, iINPR);
  and and_5 (and_5_out, com, not_1_out);
  and and_6 (and_6_out, shr, i_1_ac);
  and and_7 (and_7_out, shl, i_1_ac_2);
  or or_1 (iAC_2, and_1_out, and_2_out, and_3_out, and_4_out, and_5_out, and_6_out, and_7_out);
endmodule
