// Logisim project adder-AC-bus.circ as structural Verilog: 1 circuit, main circuit main
module main (
  input  D0,
  input  T5,
  input  D1,
  input  D2,
  input  p,
  input  b11,
  input  CLOCK,
  input  r,
  input  b9,
  input  b7,
  input  b6,
  input  b5,
  input  b11_2,
  input  E_IN,
  input  r_2,
  input  B8,
  input  E_CLR,
  input  r_3,
  input  B10,
  input  [7:0] from_INPR,
  input  [15:0] from_DR,
  output [15:0] AC_out,
  output E_OUT
);

  wire and_1_out, and_2_out, and_3_out, and_4_out, and_5_out, and_6_out, and_7_out, and_8_out, and_9_out,
       and_10_out, and_11_out, and_12_out, main_2_c_out, main_2_e_in, multiplexer_1_out, not_1_out,
       not_2_out, or_1_out, or_2_out, or_3_out, or_4_out;
  wire [15:0] main_2__0ac_prime;

  or or_1 (or_1_out, E_IN, or_4_out);
  and and_1 (and_1_out, r_2, B8);
  not not_1 (not_1_out, E_OUT);
  Multiplexer #(.enable("false")) multiplexer_1 (
    .in0(or_1_out), .in1(not_1_out), .out(multiplexer_1_out), .sel(and_1_out));
  not not_2 (not_2_out, multiplexer_1_out);
  and and_2 (and_2_out, D0, T5);
  and and_3 (and_3_out, D1, T5);
  and and_4 (and_4_out, D2, T5);
  and and_5 (and_5_out, p, b11);
  and and_6 (and_6_out, r, b9);
  and and_7 (and_7_out, r, b7);
  and and_8 (and_8_out, r, b6);
  and and_9 (and_9_out, r, b5);
  and and_10 (and_10_out, r, b11_2);
  J_K_Flip_Flop j_k_ff_1 (
    .J(multiplexer_1_out), .clk(CLOCK), .K(not_2_out), .Q(E_OUT), .reset(or_2_out));  // open: Qn, preset, en
  or or_2 (or_2_out, E_CLR, and_11_out);
  and and_11 (and_11_out, r_3, B10);
  or or_3 (or_3_out, and_2_out, and_3_out, and_4_out, and_5_out, and_6_out, and_7_out, and_8_out);
  _16bit_reg_main main_1 (
    .load(or_3_out), .INC(and_9_out), .\input (main_2__0ac_prime), .CLOCK(CLOCK), .CLR(and_10_out),
    .\output (AC_out));
  or or_4 (or_4_out, and_12_out, main_2_e_in);
  and and_12 (and_12_out, main_2_c_out, and_3_out);
  add_lc_main main_2 (
    .AND_prime(and_2_out), ._0(1'b0), .ADD_prime(and_3_out), .DR_prime(and_4_out), ._3DR(from_DR[3]),
    .INPR_prime(and_5_out), .COM_prime(and_6_out), .SHR_prime(and_7_out), .SHL_prime(and_8_out),
    ._0inpr(from_INPR[0]), ._0AC_prime(main_2__0ac_prime[0]), ._4AC_prime(main_2__0ac_prime[4]),
    ._8AC_prime(main_2__0ac_prime[8]), ._12AC_prime(main_2__0ac_prime[12]), ._1inpr(from_INPR[1]),
    ._1AC_prime(main_2__0ac_prime[1]), ._5AC_prime(main_2__0ac_prime[5]), ._9AC_prime(main_2__0ac_prime[9]),
    ._13AC_prime(main_2__0ac_prime[13]), ._2inpr(from_INPR[2]), ._2AC_prime(main_2__0ac_prime[2]),
    ._6AC_prime(main_2__0ac_prime[6]), ._10AC_prime(main_2__0ac_prime[10]),
    ._14AC_prime(main_2__0ac_prime[14]), ._3inpr(from_INPR[3]), ._3AC_prime(main_2__0ac_prime[3]),
    ._7AC_prime(main_2__0ac_prime[7]), ._11AC_prime(main_2__0ac_prime[11]),
    ._15AC_prime(main_2__0ac_prime[15]), .C_OUT(main_2_c_out), .FROM_E(E_OUT), ._0AC(AC_out[0]),
    ._1AC(AC_out[1]), ._2AC(AC_out[2]), ._3AC(AC_out[3]), ._0DR(from_DR[0]), ._1DR(from_DR[1]),
    ._2dr(from_DR[2]), ._4inpr(from_INPR[4]), ._5inpr(from_INPR[5]), ._6inpr(from_INPR[6]),
    ._7inpr(from_INPR[7]), ._4AC(AC_out[4]), ._5AC(AC_out[5]), ._6AC(AC_out[6]), ._7AC(AC_out[7]),
    ._4DR(from_DR[4]), ._5DR(from_DR[5]), ._6DR(from_DR[6]), ._7DR(from_DR[7]), ._8AC(AC_out[8]),
    ._9AC(AC_out[9]), ._10AC(AC_out[10]), ._11AC(AC_out[11]), ._8DR(from_DR[8]), ._9DR(from_DR[9]),
    ._10DR(from_DR[10]), ._11DR(from_DR[11]), .E_IN(main_2_e_in), ._12AC(AC_out[12]), ._13AC(AC_out[13]),
    ._14AC(AC_out[14]), ._15AC(AC_out[15]), ._12DR(from_DR[12]), ._13DR(from_DR[13]), ._14DR(from_DR[14]),
    ._15DR(from_DR[15]));
endmodule
