// Logisim project cpu.circ as structural Verilog: 1 circuit, main circuit main
module main (
  input  T7,
  input  [15:0] DR_OUt,
  input  [15:0] AC_OUT,
  input  D0,
  input  D1,
  input  D2,
  input  D3,
  input  D4,
  input  D5,
  input  D6,
  input  D7,
  input  T0,
  input  T1,
  input  T2,
  input  T3,
  input  T4,
  input  T5,
  input  T6,
  input  R,
  input  E,
  input  Clock,
  input  B0,
  input  B1,
  input  B2,
  input  B3,
  input  B4,
  input  B5,
  input  B6,
  input  FGI,
  input  FGO,
  input  B7,
  input  B8,
  input  B9,
  input  B10,
  input  AC_15,
  input  IR_15,
  output load_AR,
  output INC_AR,
  output load_DR,
  output INC_DR,
  output CLR_SC,
  output bus_s2,
  output bus_s1,
  output bus_S0,
  output LOAD_PC,
  output INC_PC,
  output J_S_F_F,
  output K_S_F_F,
  output P,
  output r_2
);

  wire main_6_i_out, not_1_out, not_2_out, not_4_out, p_prime_prime_out;

  not not_1 (not_1_out, D7);
  not not_2 (not_2_out, main_6_i_out);
  // NOT_Gate not_3 has open pins: in=R, out=open
  and u_p (P, T3, main_6_i_out, D7);
  and u_r (r_2, D7, T3, not_2_out);
  AR_main main_1 (
    .D7_prime(not_1_out), .I(main_6_i_out), .T3(T3), .T2(T2), .T0(T0), .D5(D5), .T4(T4), .load_AR(load_AR),
    .INC_AR(INC_AR));
  DR_main main_2 (.T4(T4), .D0(D0), .D1(D1), .D2(D2), .D6(D6), .T5(T5), .LOAd_DR(load_DR), .INC_DR(INC_DR));
  PC_main main_3 (
    .D4(D4), .T4(T4), .D5(D5), .T5(T5), .T1(T1), .DR_OUT(DR_OUt), .D6(D6), .T6(T6), .r(r_2), .AC15(AC_15),
    .B4(B4), .B3(B3), .B2(B2), .E(E), .B1(B1), .P(P), .FGI(FGI), .B9(B9), .FGO(FGO), .B8(B8),
    .AC_OUT(AC_OUT), .LOAD_PC(LOAD_PC), .INC_PC(INC_PC));
  BUS__main main_4 (
    .D0(D0), .D1(D1), .D2(D2), .D3(D3), .D4(D4), .D5(D5), .D6(D6), .D7(D7), .T0(T0), .T1(T1), .T2(T2),
    .T3(T3), .T4(T4), .T5(T5), .T6(T6), .T7(T7), .I(main_6_i_out), .P(P), .B10(B10), .S2(bus_s2),
    .S1(bus_s1), .S0(bus_S0));
  S_FF__main main_5 (.r(r_2), .B0(B0), .J_S_F_F(J_S_F_F), .K_S_F_F(K_S_F_F));
  I_FF__main main_6 (.IR_15(IR_15), .CLOCK(Clock), .T2(T2), .I_OUT(main_6_i_out));
  SC_main main_7 (
    .D0(D0), .T6(T6), .D1(D1), .D2(D2), .D3(D3), .T5(T5), .D4(D4), .D5(D5), .D6(D6), .T7(T7),
    .r_prime_prime(r_2), .P_prime_prime(p_prime_prime_out), .SC_CLR(CLR_SC));
  and r_prime_prime (r_2, D7, T4, not_4_out);
  and p_prime_prime (p_prime_prime_out, main_6_i_out, D7, T4);
  not not_4 (not_4_out, main_6_i_out);
endmodule
